# Fritzing sketch MuscleWire (saved by Fritzing 0.7.10b)
breadboards: 1

parts:
  R1 = Resistor [tolerance=±5% resistance=1k package=THT]
  Arduino2 = Arduino
  D1 = Rectifier Diode [part_number=1N4001 package="300 mil [THT]"]
  Q1 = Basic FET N-Channel [package="TO220 [THT]"]
  VCC1 = Battery

nets:
  N1: R1.Pin_0, Arduino2.D3
  N2: R1.Pin_1, Q1.gate
  N3: Arduino2.GND, D1.anode, Q1.source, VCC1.-
  N4: D1.cathode, Q1.drain

notes:
  One end of the Muscle Wire gets connected here
  These are D-cell batteries
