# Fritzing sketch proximity (saved by Fritzing 0.7.10b)
breadboards: 1

parts:
  Arduino2 = Arduino
  J1 = Infrared Proximity Sensor
  R4 = Resistor [tolerance=±5% resistance=100 package=THT]
  R5 = Resistor [tolerance=±5% resistance=100 package=THT]
  R6 = Resistor [tolerance=±5% resistance=330 package=THT]
  LED1 = RGB LED (com. anode, rbg) [package="5 mm [THT]"]

nets:
  N1: Arduino2.D11, R6.Pin_0
  N2: Arduino2.D10, R5.Pin_0
  N3: Arduino2.D9, R4.Pin_0
  +5V: Arduino2.+5V, J1.Vcc
  GND: Arduino2.GND, J1.GND, LED1.common_anode
  N4: Arduino2.A0, J1.Vout
  N5: R4.Pin_1, LED1.green_cathode
  N6: R5.Pin_1, LED1.blue_cathode
  N7: R6.Pin_1, LED1.red_cathode
