# Fritzing sketch stretch (saved by Fritzing 0.7.10b)
breadboards: 1

parts:
  R1 = Resistor [tolerance=±5% resistance=10 package=THT]
  J1 = Piezo Speaker
  Arduino2 = Arduino

nets:
  N1: R1.Pin_0, Arduino2.A0
  N2: R1.Pin_1, J1.pin1, Arduino2.GND
  N3: J1.pin2, Arduino2.D9

notes:
  stretch sensor gets connected here...
