# Fritzing sketch vibro (saved by Fritzing 0.7.10b)
breadboards: 1

parts:
  Arduino2 = Arduino
  R3 = Rotary Potentiometer (Large) [package=THT]

nets:
  N1: Arduino2.+5V, R3.leg1
  N2: Arduino2.GND, R3.leg2
  N3: Arduino2.A0, R3.wiper

notes:
  Connect your vibration motor leads here. Red to pin 3. Black to gnd.
